# Fritzing sketch pbox (saved by Fritzing 0.8.3b)
breadboards: 1

parts:
  Part1 = Arduino Uno (Rev3)
  LCD1 = LCD screen
  BAT1 = BC9VPC [package=bc9vpc]
  J1 = Basic Servo
  S2 = Round Pushbutton

nets:
  N1: Part1.ICSP_MISO, Part1.D12/MISO, LCD1.RS
  N2: Part1.ICSP_MOSI, Part1.D11_PWM/MOSI, LCD1.E
  GND: Part1.GND, LCD1.VSS, LCD1.V0, LCD1.R/W, LCD1.LED-, BAT1.V+, J1.gnd, S2.leg0
  N3: Part1.D9_PWM, J1.pulse
  N4: Part1.D13/SCK, S2.leg1
  N5: Part1.D2, LCD1.DB7
  N6: Part1.D3_PWM, LCD1.DB6
  N7: Part1.D4, LCD1.DB5
  N8: Part1.D5_PWM, LCD1.DB4
  N9: Part1.D7, LCD1.LED+
  5V: Part1.5V, LCD1.VDD, BAT1.V-, J1.vcc
